# Fritzing sketch 7SegmentDriver (saved by Fritzing 0.9.9b)
breadboards: 1

parts:
  IC1 = ULN2003A [package="SO16 [SMD]"]
  7_Segment1 = 7 Segment Display
  U1 = 74HC595 [package="DIP16 [THT]"]
  Part1 = Arduino Nano (Rev3.0)
  VCC1 = Battery block 9V

nets:
  N1: IC1.In_1, U1.Q7
  N2: IC1.In_2, U1.Q6
  N3: IC1.In_3, U1.Q5
  N4: IC1.In_4, U1.Q4
  N5: IC1.In_5, U1.Q3
  N6: IC1.In_6, U1.Q2
  N7: IC1.In_7, U1.Q1
  GND: IC1.0V, IC1.COM_-_Common, U1.GND, U1.OE, Part1.GND, VCC1.-
  N8: IC1.Out_7, 7_Segment1.Segment_E
  N9: IC1.Out_6, 7_Segment1.Segment_F
  N10: IC1.Out_5, 7_Segment1.Segment_A
  N11: IC1.Out_4, 7_Segment1.Segment_B
  N12: IC1.Out_3, 7_Segment1.Segment_G
  N13: IC1.Out_2, 7_Segment1.common_anode#12
  N14: IC1.Out_1, 7_Segment1.Segment_D
  N15: 7_Segment1.common_anode#3, 7_Segment1.common_anode#5, 7_Segment1.common_anode#11, 7_Segment1.common_anode#16, Part1.VIN, VCC1.+
  N16: U1.MR, U1.Q0, Part1.5V
  N17: U1.SH_CP, Part1.D6
  N18: U1.ST_CP, Part1.D5
  N19: U1.DS, Part1.D4
