# Fritzing sketch 7SegmentDriver_2 (saved by Fritzing 0.9.9b)
perfboards: 1

parts:
  JP1 = Header 6 [package=1x06_smd_straight_alt]
  JP2 = Header 6 [package=1x06_smd_straight_alt]
  IC1 = ULN2003A [package="DIP16 [THT]"]
  U1 = 74HC595 [package="DIP16 [THT]"]
  JP3 = Header 6 [package=1x06_smd_straight_alt]
  Q1 = TRANSISTOR_NPN [package=to-92-ammo]
  R2 = Vertical Resistor [tolerance=±5% resistance=220 package=THT]
  R3 = Vertical Resistor [tolerance=±5% resistance=220 package=THT]
  R4 = Vertical Resistor [tolerance=±5% resistance=220 package=THT]
  R5 = Vertical Resistor [tolerance=±5% resistance=220 package=THT]
  R6 = Vertical Resistor [tolerance=±5% resistance=220 package=THT]
  R7 = Vertical Resistor [tolerance=±5% resistance=220 package=THT]
  R8 = Vertical Resistor [tolerance=±5% resistance=220 package=THT]
  R9 = Vertical Resistor [tolerance=±5% resistance=10k package=THT]
  R10 = Vertical Resistor [tolerance=±5% resistance=330 package=THT]
  7_Segment1 = 7 Segment Display
  JP4 = Header 6 [package=1x06_smd_straight_alt]

nets:
  N1: JP1.2, R2.Pin_1, 7_Segment1.Segment_G
  N2: JP1.3, R4.Pin_1, 7_Segment1.Segment_F
  N3: JP1.5, R8.Pin_1, 7_Segment1.Segment_A
  N4: JP1.6, R7.Pin_1, 7_Segment1.Segment_B
  N5: JP2.2, R3.Pin_1, 7_Segment1.Segment_E
  N6: JP2.3, R5.Pin_1, 7_Segment1.Segment_D
  N7: JP2.4, JP3.6, 7_Segment1.common_anode, JP4.6
  N8: JP2.5, R6.Pin_1, 7_Segment1.Segment_C
  N9: JP2.6, Q1.E, 7_Segment1.Segment_DP
  N10: IC1.In_1, U1.Q7
  N11: IC1.In_2, U1.Q6
  N12: IC1.In_3, U1.Q5
  N13: IC1.In_4, U1.Q4
  N14: IC1.In_5, U1.Q3
  N15: IC1.In_6, U1.Q2
  N16: IC1.In_7, U1.Q1
  N17: IC1.0V, IC1.COM_-_Common, U1.GND, U1.OE, JP3.4, R10.Pin_0, JP4.4
  N18: IC1.Out_7, R8.Pin_0
  N19: IC1.Out_6, R7.Pin_0
  N20: IC1.Out_5, R6.Pin_0
  N21: IC1.Out_4, R5.Pin_0
  N22: IC1.Out_3, R3.Pin_0
  N23: IC1.Out_2, R4.Pin_0
  N24: IC1.Out_1, R2.Pin_0
  N25: U1.Q7', JP4.3
  N26: U1.MR, U1.VCC, JP3.5, JP4.5
  N27: U1.SH_CP, JP3.1, JP4.1
  N28: U1.ST_CP, JP3.2, JP4.2
  N29: U1.DS, JP3.3
  N30: U1.Q0, R9.Pin_1
  N31: Q1.B, R9.Pin_0
  N32: Q1.C, R10.Pin_1

custom parts:
  Vertical Resistor: A generic resistor (0.25W)
