# Fritzing sketch 7SegmentDriver_3 (saved by Fritzing 0.9.9b)
perfboards: 1

parts:
  IC1 = ULN2003A [package="DIP16 [THT]"]
  U1 = 74HC595 [package="DIP16 [THT]"]
  JP3 = Header 6 [package=1x06_smd_straight_alt]
  Q1 = TRANSISTOR_NPN [package=to-92-ammo]
  R2 = Vertical Resistor [tolerance=±5% resistance=220 package=THT]
  R3 = Vertical Resistor [tolerance=±5% resistance=220 package=THT]
  R4 = Vertical Resistor [tolerance=±5% resistance=220 package=THT]
  R5 = Vertical Resistor [tolerance=±5% resistance=220 package=THT]
  R6 = Vertical Resistor [tolerance=±5% resistance=220 package=THT]
  R7 = Vertical Resistor [tolerance=±5% resistance=220 package=THT]
  R8 = Vertical Resistor [tolerance=±5% resistance=220 package=THT]
  R9 = Vertical Resistor [tolerance=±5% resistance=10k package=THT]
  R10 = Vertical Resistor [tolerance=±5% resistance=330 package=THT]
  7_Segment1 = 7 Segment Display
  JP4 = Header 6 [package=1x06_smd_straight_alt]
  JP2 = Header 10 [package=1x10-2mm-smd]
  Power_plug1 = Power plug
  Part1 = Arduino Nano (Rev3.0)
  JP5 = Header 6 [package=1x06_smd_straight_alt]

nets:
  N1: IC1.In_1, U1.Q7
  N2: IC1.In_2, U1.Q6
  N3: IC1.In_3, U1.Q5
  N4: IC1.In_4, U1.Q4
  N5: IC1.In_5, U1.Q3
  N6: IC1.In_6, U1.Q2
  N7: IC1.In_7, U1.Q1
  GND: IC1.0V, U1.GND, U1.OE, JP3.5, Q1.E, JP4.5, Power_plug1.GND, Part1.GND, JP5.5
  N8: IC1.Out_7, R8.Pin_0
  N9: IC1.Out_6, R7.Pin_0
  N10: IC1.Out_5, R6.Pin_0
  N11: IC1.Out_4, R5.Pin_0
  N12: IC1.Out_3, R3.Pin_0
  N13: IC1.Out_2, R4.Pin_0
  N14: IC1.Out_1, R2.Pin_0
  N15: U1.Q7', JP5.1
  VCC: U1.MR, U1.VCC, JP3.2, JP4.2, Part1.5V, JP5.2
  N16: U1.SH_CP, JP3.3, JP4.3, Part1.D7, JP5.3
  N17: U1.ST_CP, JP3.4, JP4.4, Part1.D6, JP5.4
  N18: U1.DS, JP3.1, JP4.1, Part1.D5
  N19: U1.Q0, R9.Pin_1
  N20: JP3.6, R6.Pin_1, 7_Segment1.common_anode, JP4.6, JP2.6, JP2.10, Power_plug1.VCC, JP5.6
  N21: Q1.B, R9.Pin_0
  N22: Q1.C, R10.Pin_0
  N23: R2.Pin_1, 7_Segment1.Segment_A, JP2.2
  N24: R3.Pin_1, 7_Segment1.Segment_G, JP2.4
  N25: R4.Pin_1, 7_Segment1.Segment_F, JP2.3
  N26: R5.Pin_1, JP2.5
  N27: R7.Pin_1, 7_Segment1.Segment_C, JP2.7
  N28: R8.Pin_1, 7_Segment1.Segment_B, JP2.8
  N29: R10.Pin_1, 7_Segment1.Segment_DP, JP2.1

custom parts:
  Vertical Resistor: A generic resistor (0.25W)
